// Logisim project Four_Bits_Add_Sub.circ as structural Verilog: 2 circuits, main circuit Add_Sub_4Bits
module Add_Sub_4Bits (
  input  [3:0] A,
  input  [3:0] B,
  input  Add_Sub,
  output [3:0] R,
  output Zero,
  output Overflow
);

  wire add_1bit_1_cout, add_1bit_2_cout, add_1bit_3_cout, add_1bit_4_cout, and_1_out, and_2_out, and_3_out,
       and_4_out, and_5_out, and_6_out, and_7_out, and_8_out, and_9_out, and_10_out, and_11_out, not_1_out,
       not_2_out, not_3_out, not_4_out, not_5_out, or_1_out, or_2_out, or_3_out, or_4_out, xor_1_out,
       xor_2_out, xor_3_out, xor_4_out;

  // Probe on A
  not not_1 (not_1_out, B[3]);
  not not_2 (not_2_out, B[1]);
  not not_3 (not_3_out, B[2]);
  not not_4 (not_4_out, B[0]);
  and and_1 (and_1_out, not_4_out, not_5_out);
  and and_2 (and_2_out, not_2_out, and_1_out);
  and and_3 (and_3_out, not_3_out, and_2_out);
  // Probe on B
  and and_4 (and_4_out, B[3], Add_Sub);
  not not_5 (not_5_out, Add_Sub);
  xor xor_1 (xor_1_out, not_5_out, not_4_out);
  xor xor_2 (xor_2_out, and_1_out, not_2_out);
  xor xor_3 (xor_3_out, and_2_out, not_3_out);
  xor xor_4 (xor_4_out, and_3_out, not_1_out);
  and and_5 (and_5_out, B[0], Add_Sub);
  and and_6 (and_6_out, B[2], Add_Sub);
  and and_7 (and_7_out, B[1], Add_Sub);
  or or_1 (or_1_out, and_5_out, and_8_out);
  and and_8 (and_8_out, not_5_out, xor_1_out);
  or or_2 (or_2_out, and_7_out, and_9_out);
  and and_9 (and_9_out, not_5_out, xor_2_out);
  or or_3 (or_3_out, and_6_out, and_10_out);
  and and_10 (and_10_out, not_5_out, xor_3_out);
  or or_4 (or_4_out, and_4_out, and_11_out);
  and and_11 (and_11_out, not_5_out, xor_4_out);
  // Probe on R
  and and_12 (Zero, ~R[0], ~R[1], ~R[2], ~R[3], ~Overflow);  // AND_Gate
  Add_1Bit add_1bit_1 (.A(A[0]), .Cout(add_1bit_1_cout), .B(or_1_out), .Sum(R[0]), .Cin(1'b0));
  Add_1Bit add_1bit_2 (.A(A[1]), .Cout(add_1bit_2_cout), .B(or_2_out), .Sum(R[1]), .Cin(add_1bit_1_cout));
  Add_1Bit add_1bit_3 (.A(A[2]), .Cout(add_1bit_3_cout), .B(or_3_out), .Sum(R[2]), .Cin(add_1bit_2_cout));
  Add_1Bit add_1bit_4 (.A(A[3]), .Cout(add_1bit_4_cout), .B(or_4_out), .Sum(R[3]), .Cin(add_1bit_3_cout));
  xor xor_5 (Overflow, add_1bit_4_cout, add_1bit_3_cout);

  // Notes on the sheet:
  //   LE, Nhat Hung; 260793376
endmodule

module Add_1Bit (
  input  Cin,
  input  A,
  input  B,
  output Sum,
  output Cout
);

  wire and_1_out, and_2_out, xor_1_out;

  xor xor_1 (xor_1_out, A, B);
  and and_1 (and_1_out, B, A);
  xor xor_2 (Sum, Cin, xor_1_out);
  and and_2 (and_2_out, Cin, xor_1_out);
  or or_1 (Cout, and_2_out, and_1_out);

  // Notes on the sheet:
  //   YOUR NAME AND STUDENT NUMBER HERE
  //   MAKE SURE THAT YOU OPENED THIS PROJECT IN "LOGISIM-EVOLUTION"
  //   YOU CAN FIND "LOGISIM-EVOLUTION" PROGRAM IN THE ASSIGNMENT'S FOLDER
  //   DO NOT USE "LOGISIM" VERSION TO SOLVE THIS ASSIGNMENT!
endmodule
