// Logisim project RAM_16_Nibbles_Read_Write.circ as structural Verilog: 2 circuits, main circuit RAM_16_Nibbles
// Clk
module RAM_16_Nibbles (
  input  [3:0] Data,
  input  [3:0] Address,
  input  Read_Write,
  output [3:0] RAM_OUT
);

  wire and_1_out, and_2_out, and_3_out, and_4_out, and_5_out, and_6_out, and_7_out, and_8_out, and_9_out,
       and_10_out, and_11_out, and_12_out, and_13_out, and_14_out, and_15_out, and_16_out, Clk_out;
  wire [3:0] and_17_out, and_21_out, and_25_out, and_29_out, and_33_out, and_37_out, and_41_out, and_45_out,
       and_49_out, and_53_out, and_57_out, and_61_out, and_65_out, and_69_out, and_73_out, and_77_out,
       nibble_1_nibble_out, nibble_2_nibble_out, nibble_3_nibble_out, nibble_4_nibble_out,
       nibble_5_nibble_out, nibble_6_nibble_out, nibble_7_nibble_out, nibble_8_nibble_out,
       nibble_9_nibble_out, nibble_10_nibble_out, nibble_11_nibble_out, nibble_12_nibble_out,
       nibble_13_nibble_out, nibble_14_nibble_out, nibble_15_nibble_out, nibble_16_nibble_out;

  // Probe on Data
  Clock Clk (.out(Clk_out));
  // Probe on Address
  and and_1 (and_1_out, ~Address[0], ~Address[1], ~Address[2], ~Address[3]);  // AND_Gate
  and and_2 (and_2_out, Address[0], ~Address[1], ~Address[2], ~Address[3]);  // AND_Gate
  and and_3 (and_3_out, ~Address[0], Address[1], ~Address[2], ~Address[3]);  // AND_Gate
  and and_4 (and_4_out, Address[0], Address[1], ~Address[2], ~Address[3]);  // AND_Gate
  and and_5 (and_5_out, ~Address[0], ~Address[1], Address[2], ~Address[3]);  // AND_Gate
  and and_6 (and_6_out, Address[0], ~Address[1], Address[2], ~Address[3]);  // AND_Gate
  and and_7 (and_7_out, ~Address[0], Address[1], Address[2], ~Address[3]);  // AND_Gate
  and and_8 (and_8_out, Address[0], Address[1], Address[2], ~Address[3]);  // AND_Gate
  and and_9 (and_9_out, ~Address[0], ~Address[1], ~Address[2], Address[3]);  // AND_Gate
  and and_10 (and_10_out, Address[0], ~Address[1], ~Address[2], Address[3]);  // AND_Gate
  and and_11 (and_11_out, ~Address[0], Address[1], ~Address[2], Address[3]);  // AND_Gate
  and and_12 (and_12_out, Address[0], Address[1], ~Address[2], Address[3]);  // AND_Gate
  and and_13 (and_13_out, ~Address[0], ~Address[1], Address[2], Address[3]);  // AND_Gate
  and and_14 (and_14_out, Address[0], ~Address[1], Address[2], Address[3]);  // AND_Gate
  and and_15 (and_15_out, ~Address[0], Address[1], Address[2], Address[3]);  // AND_Gate
  and and_16 (and_16_out, Address[0], Address[1], Address[2], Address[3]);
  Nibble nibble_1 (
    .Data(Data), .Read_Write(Read_Write), .Enable(and_1_out), .Clk(Clk_out), .Nibble_Out(nibble_1_nibble_out));
  Nibble nibble_2 (
    .Data(Data), .Read_Write(Read_Write), .Enable(and_2_out), .Clk(Clk_out), .Nibble_Out(nibble_2_nibble_out));
  Nibble nibble_3 (
    .Data(Data), .Read_Write(Read_Write), .Enable(and_3_out), .Clk(Clk_out), .Nibble_Out(nibble_3_nibble_out));
  Nibble nibble_4 (
    .Data(Data), .Read_Write(Read_Write), .Enable(and_4_out), .Clk(Clk_out), .Nibble_Out(nibble_4_nibble_out));
  Nibble nibble_5 (
    .Data(Data), .Read_Write(Read_Write), .Enable(and_5_out), .Clk(Clk_out), .Nibble_Out(nibble_5_nibble_out));
  Nibble nibble_6 (
    .Data(Data), .Read_Write(Read_Write), .Enable(and_6_out), .Clk(Clk_out), .Nibble_Out(nibble_6_nibble_out));
  Nibble nibble_7 (
    .Data(Data), .Read_Write(Read_Write), .Enable(and_7_out), .Clk(Clk_out), .Nibble_Out(nibble_7_nibble_out));
  Nibble nibble_8 (
    .Data(Data), .Read_Write(Read_Write), .Enable(and_8_out), .Clk(Clk_out), .Nibble_Out(nibble_8_nibble_out));
  Nibble nibble_9 (
    .Data(Data), .Read_Write(Read_Write), .Enable(and_9_out), .Clk(Clk_out), .Nibble_Out(nibble_9_nibble_out));
  Nibble nibble_10 (
    .Data(Data), .Read_Write(Read_Write), .Enable(and_10_out), .Clk(Clk_out),
    .Nibble_Out(nibble_10_nibble_out));
  Nibble nibble_11 (
    .Data(Data), .Read_Write(Read_Write), .Enable(and_11_out), .Clk(Clk_out),
    .Nibble_Out(nibble_11_nibble_out));
  Nibble nibble_12 (
    .Data(Data), .Read_Write(Read_Write), .Enable(and_12_out), .Clk(Clk_out),
    .Nibble_Out(nibble_12_nibble_out));
  Nibble nibble_13 (
    .Data(Data), .Read_Write(Read_Write), .Enable(and_13_out), .Clk(Clk_out),
    .Nibble_Out(nibble_13_nibble_out));
  Nibble nibble_14 (
    .Data(Data), .Read_Write(Read_Write), .Enable(and_14_out), .Clk(Clk_out),
    .Nibble_Out(nibble_14_nibble_out));
  Nibble nibble_15 (
    .Data(Data), .Read_Write(Read_Write), .Enable(and_15_out), .Clk(Clk_out),
    .Nibble_Out(nibble_15_nibble_out));
  Nibble nibble_16 (
    .Data(Data), .Read_Write(Read_Write), .Enable(and_16_out), .Clk(Clk_out),
    .Nibble_Out(nibble_16_nibble_out));
  and and_17 (and_17_out[0], Read_Write, nibble_1_nibble_out[0]);
  and and_18 (and_17_out[1], nibble_1_nibble_out[1], Read_Write);
  and and_19 (and_17_out[2], Read_Write, nibble_1_nibble_out[2]);
  and and_20 (and_17_out[3], nibble_1_nibble_out[3], Read_Write);
  and and_21 (and_21_out[0], Read_Write, nibble_2_nibble_out[0]);
  and and_22 (and_21_out[1], nibble_2_nibble_out[1], Read_Write);
  and and_23 (and_21_out[2], Read_Write, nibble_2_nibble_out[2]);
  and and_24 (and_21_out[3], nibble_2_nibble_out[3], Read_Write);
  and and_25 (and_25_out[0], Read_Write, nibble_3_nibble_out[0]);
  and and_26 (and_25_out[1], nibble_3_nibble_out[1], Read_Write);
  and and_27 (and_25_out[2], Read_Write, nibble_3_nibble_out[2]);
  and and_28 (and_25_out[3], nibble_3_nibble_out[3], Read_Write);
  and and_29 (and_29_out[0], Read_Write, nibble_4_nibble_out[0]);
  and and_30 (and_29_out[1], nibble_4_nibble_out[1], Read_Write);
  and and_31 (and_29_out[2], Read_Write, nibble_4_nibble_out[2]);
  and and_32 (and_29_out[3], nibble_4_nibble_out[3], Read_Write);
  and and_33 (and_33_out[0], Read_Write, nibble_5_nibble_out[0]);
  and and_34 (and_33_out[1], nibble_5_nibble_out[1], Read_Write);
  and and_35 (and_33_out[2], Read_Write, nibble_5_nibble_out[2]);
  and and_36 (and_33_out[3], nibble_5_nibble_out[3], Read_Write);
  and and_37 (and_37_out[0], Read_Write, nibble_6_nibble_out[0]);
  and and_38 (and_37_out[1], nibble_6_nibble_out[1], Read_Write);
  and and_39 (and_37_out[2], Read_Write, nibble_6_nibble_out[2]);
  and and_40 (and_37_out[3], nibble_6_nibble_out[3], Read_Write);
  and and_41 (and_41_out[0], Read_Write, nibble_7_nibble_out[0]);
  and and_42 (and_41_out[1], nibble_7_nibble_out[1], Read_Write);
  and and_43 (and_41_out[2], Read_Write, nibble_7_nibble_out[2]);
  and and_44 (and_41_out[3], nibble_7_nibble_out[3], Read_Write);
  and and_45 (and_45_out[0], Read_Write, nibble_8_nibble_out[0]);
  and and_46 (and_45_out[1], nibble_8_nibble_out[1], Read_Write);
  and and_47 (and_45_out[2], Read_Write, nibble_8_nibble_out[2]);
  and and_48 (and_45_out[3], nibble_8_nibble_out[3], Read_Write);
  and and_49 (and_49_out[0], Read_Write, nibble_9_nibble_out[0]);
  and and_50 (and_49_out[1], nibble_9_nibble_out[1], Read_Write);
  and and_51 (and_49_out[2], Read_Write, nibble_9_nibble_out[2]);
  and and_52 (and_49_out[3], nibble_9_nibble_out[3], Read_Write);
  and and_53 (and_53_out[0], Read_Write, nibble_10_nibble_out[0]);
  and and_54 (and_53_out[1], nibble_10_nibble_out[1], Read_Write);
  and and_55 (and_53_out[2], Read_Write, nibble_10_nibble_out[2]);
  and and_56 (and_53_out[3], nibble_10_nibble_out[3], Read_Write);
  and and_57 (and_57_out[0], Read_Write, nibble_11_nibble_out[0]);
  and and_58 (and_57_out[1], nibble_11_nibble_out[1], Read_Write);
  and and_59 (and_57_out[2], Read_Write, nibble_11_nibble_out[2]);
  and and_60 (and_57_out[3], nibble_11_nibble_out[3], Read_Write);
  and and_61 (and_61_out[0], Read_Write, nibble_12_nibble_out[0]);
  and and_62 (and_61_out[1], nibble_12_nibble_out[1], Read_Write);
  and and_63 (and_61_out[2], Read_Write, nibble_12_nibble_out[2]);
  and and_64 (and_61_out[3], nibble_12_nibble_out[3], Read_Write);
  and and_65 (and_65_out[0], Read_Write, nibble_13_nibble_out[0]);
  and and_66 (and_65_out[1], nibble_13_nibble_out[1], Read_Write);
  and and_67 (and_65_out[2], Read_Write, nibble_13_nibble_out[2]);
  and and_68 (and_65_out[3], nibble_13_nibble_out[3], Read_Write);
  and and_69 (and_69_out[0], Read_Write, nibble_14_nibble_out[0]);
  and and_70 (and_69_out[1], nibble_14_nibble_out[1], Read_Write);
  and and_71 (and_69_out[2], Read_Write, nibble_14_nibble_out[2]);
  and and_72 (and_69_out[3], nibble_14_nibble_out[3], Read_Write);
  and and_73 (and_73_out[0], Read_Write, nibble_15_nibble_out[0]);
  and and_74 (and_73_out[1], nibble_15_nibble_out[1], Read_Write);
  and and_75 (and_73_out[2], Read_Write, nibble_15_nibble_out[2]);
  and and_76 (and_73_out[3], nibble_15_nibble_out[3], Read_Write);
  and and_77 (and_77_out[0], Read_Write, nibble_16_nibble_out[0]);
  and and_78 (and_77_out[1], nibble_16_nibble_out[1], Read_Write);
  and and_79 (and_77_out[2], Read_Write, nibble_16_nibble_out[2]);
  and and_80 (and_77_out[3], nibble_16_nibble_out[3], Read_Write);
  // Probe on RAM_OUT
  assign RAM_OUT = and_17_out | and_21_out | and_25_out | and_29_out | and_33_out | and_37_out | and_41_out | and_45_out | and_49_out | and_53_out | and_57_out | and_61_out | and_65_out | and_69_out | and_73_out | and_77_out;  // OR_Gate or_1, 4 bits wide

  // Notes on the sheet:
  //   When Read_Write = 1 performs read, otherwise performs write
endmodule

module Nibble (
  input  [3:0] Data,
  input  Read_Write,
  input  Enable,
  input  Clk,
  output [3:0] Nibble_Out
);

  wire and_1_out, and_2_out, and_3_out, and_4_out, and_5_out, and_6_out, and_7_out, and_8_out, and_9_out,
       nor_2_out, nor_4_out, nor_6_out, nor_8_out, or_1_out;

  // Probe on Data
  and and_1 (and_1_out, ~Read_Write, Enable);  // AND_Gate
  or or_1 (or_1_out, Read_Write, and_1_out);
  and and_2 (and_2_out, ~Data[0], Clk, or_1_out);  // AND_Gate
  and and_3 (and_3_out, Data[0], Clk, or_1_out);
  and and_4 (and_4_out, ~Data[1], Clk, or_1_out);  // AND_Gate
  and and_5 (and_5_out, Data[1], Clk, or_1_out);
  and and_6 (and_6_out, ~Data[2], Clk, or_1_out);  // AND_Gate
  and and_7 (and_7_out, Data[2], Clk, or_1_out);
  and and_8 (and_8_out, ~Data[3], Clk, or_1_out);  // AND_Gate
  and and_9 (and_9_out, Data[3], Clk, or_1_out);
  nor nor_1 (Nibble_Out[0], and_2_out, nor_2_out);
  nor nor_2 (nor_2_out, Nibble_Out[0], and_3_out);
  nor nor_3 (Nibble_Out[1], and_4_out, nor_4_out);
  nor nor_4 (nor_4_out, Nibble_Out[1], and_5_out);
  nor nor_5 (Nibble_Out[2], and_6_out, nor_6_out);
  nor nor_6 (nor_6_out, Nibble_Out[2], and_7_out);
  nor nor_7 (Nibble_Out[3], and_8_out, nor_8_out);
  nor nor_8 (nor_8_out, Nibble_Out[3], and_9_out);
  // Probe on Nibble_Out

  // Notes on the sheet:
  //   When Read_Write = 1 performs read, otherwise performs write
endmodule
