// Logisim project Question_3.circ as structural Verilog: 4 circuits, main circuit main
module main (
  input  [1:0] OP_input,
  input  [2:0] S_input,
  input  [2:0] D_input,
  input  [3:0] R1_input,
  input  [3:0] R2_input,
  input  in_6,
  input  in_7
);

  wire Clk_out;
  wire [1:0] ir_1_op_out, or_7_out;
  wire [2:0] ir_1_d_out, ir_1_s_out, or_8_out, or_9_out;
  wire [3:0] and_5_out, and_6_out, and_7_out, and_8_out, and_9_out, and_10_out, or_1_out, or_2_out, or_3_out,
       or_4_out, or_5_out, or_6_out, R1_nibble_out, R2_nibble_out;
  wire [3:3] and_1_out, and_2_out, and_3_out, and_4_out, cu_1_out_1, cu_1_out_2;

  Clock Clk (.out(Clk_out));
  // Probe on R1_nibble_out
  // Probe on R2_nibble_out
  and and_1 (and_1_out[3], ~or_8_out[2], ~or_8_out[1], ~or_8_out[0]);  // AND_Gate
  and and_2 (and_2_out[3], ~or_8_out[2], ~or_8_out[1], or_8_out[0]);  // AND_Gate
  and and_3 (and_3_out[3], or_7_out[0], or_7_out[1]);
  and and_4 (and_4_out[3], or_7_out[0], or_7_out[1]);
  assign and_5_out = {in_6, or_9_out} & {4{and_1_out[3]}} & {4{and_3_out[3]}};  // AND_Gate and_5, 4 bits wide
  assign and_6_out = or_5_out & and_10_out;  // AND_Gate and_6, 4 bits wide
  assign and_7_out = {in_7, or_9_out} & {4{and_2_out[3]}} & {4{and_4_out[3]}};  // AND_Gate and_7, 4 bits wide
  assign and_8_out = or_6_out & and_9_out;  // AND_Gate and_8, 4 bits wide
  assign or_1_out = R1_input | and_5_out | and_6_out;  // OR_Gate or_1, 4 bits wide
  assign or_2_out = R2_input | and_7_out | and_8_out;  // OR_Gate or_2, 4 bits wide
  IR ir_1 (
    .D_In(D_input), .S_In(S_input), .OP_In(OP_input), .Clk(Clk_out), .OP_Out(ir_1_op_out),
    .S_Out(ir_1_s_out), .D_Out(ir_1_d_out));
  CU cu_1 (.OP_In(or_7_out), .S_In(or_8_out), .D_In(or_9_out), .out_1(cu_1_out_1[3]), .out_2(cu_1_out_2[3]));
  Nibble_Register R1 (.Nibble_In(or_1_out), .Clk(Clk_out), .Nibble_Out(R1_nibble_out));
  Nibble_Register R2 (.Nibble_In(or_2_out), .Clk(Clk_out), .Nibble_Out(R2_nibble_out));
  assign or_3_out = R1_nibble_out | 4'b0000;  // OR_Gate or_3, 4 bits wide
  assign or_4_out = R2_nibble_out | 4'b0000;  // OR_Gate or_4, 4 bits wide
  assign and_9_out = {4{cu_1_out_2[3]}} & or_3_out;  // AND_Gate and_9, 4 bits wide
  assign and_10_out = {4{cu_1_out_1[3]}} & or_4_out;  // AND_Gate and_10, 4 bits wide
  assign or_5_out = {4{cu_1_out_1[3]}} | 4'b0000;  // OR_Gate or_5, 4 bits wide
  assign or_6_out = {4{cu_1_out_2[3]}} | 4'b0000;  // OR_Gate or_6, 4 bits wide
  assign or_7_out = ir_1_op_out | 2'b00;  // OR_Gate or_7, 2 bits wide
  assign or_8_out = ir_1_s_out | 3'b000;  // OR_Gate or_8, 3 bits wide
  assign or_9_out = ir_1_d_out | 3'b000;  // OR_Gate or_9, 3 bits wide

  // Notes on the sheet:
  //   R1_input and R2_input only added for ease of grading.
  //   LEAVE ONE OF THE TWO INPUTS AT 0000 FOR THIS TO WORK CORRECTLY.
endmodule

module IR (
  input  [2:0] D_In,
  input  [2:0] S_In,
  input  [1:0] OP_In,
  input  Clk,
  output [1:0] OP_Out,
  output [2:0] S_Out,
  output [2:0] D_Out
);

  wire not_1_out, not_2_out, not_3_out, not_4_out, not_5_out, not_6_out, not_7_out, not_8_out;

  S_R_Flip_Flop s_r_ff_1 (.S(OP_In[0]), .R(not_1_out), .clk(Clk), .Q(OP_Out[0]));  // open: reset, Qn, preset
  not not_1 (not_1_out, OP_In[0]);
  S_R_Flip_Flop s_r_ff_2 (.S(OP_In[1]), .R(not_2_out), .clk(Clk), .Q(OP_Out[1]));  // open: reset, Qn, preset
  not not_2 (not_2_out, OP_In[1]);
  S_R_Flip_Flop s_r_ff_3 (.S(S_In[0]), .R(not_3_out), .clk(Clk), .Q(S_Out[0]));  // open: reset, Qn, preset
  not not_3 (not_3_out, S_In[0]);
  S_R_Flip_Flop s_r_ff_4 (.S(S_In[1]), .R(not_4_out), .clk(Clk), .Q(S_Out[1]));  // open: reset, Qn, preset
  not not_4 (not_4_out, S_In[1]);
  S_R_Flip_Flop s_r_ff_5 (.S(S_In[2]), .R(not_5_out), .clk(Clk), .Q(S_Out[2]));  // open: reset, Qn, preset
  not not_5 (not_5_out, S_In[2]);
  S_R_Flip_Flop s_r_ff_6 (.S(D_In[0]), .R(not_6_out), .clk(Clk), .Q(D_Out[0]));  // open: reset, Qn, preset
  not not_6 (not_6_out, D_In[0]);
  S_R_Flip_Flop s_r_ff_7 (.S(D_In[1]), .R(not_7_out), .clk(Clk), .Q(D_Out[1]));  // open: reset, Qn, preset
  not not_7 (not_7_out, D_In[1]);
  S_R_Flip_Flop s_r_ff_8 (.S(D_In[2]), .R(not_8_out), .clk(Clk), .Q(D_Out[2]));  // open: reset, Qn, preset
  not not_8 (not_8_out, D_In[2]);
endmodule

module CU (
  input  [1:0] OP_In,
  input  [2:0] S_In,
  input  [2:0] D_In,
  output out_1,
  output out_2
);

  wire a_out, and_1_out, and_2_out, and_3_out, and_4_out, and_5_out, b_out, c_out, d_out;

  and and_1 (and_1_out, ~OP_In[1], ~OP_In[0]);  // AND_Gate
  and and_2 (and_2_out, ~S_In[2], ~S_In[1], ~S_In[0]);  // AND_Gate
  and and_3 (and_3_out, ~S_In[2], ~S_In[1], S_In[0]);  // AND_Gate
  and and_4 (and_4_out, ~D_In[2], ~D_In[1], D_In[0]);  // AND_Gate
  and and_5 (and_5_out, ~D_In[2], ~D_In[1], ~D_In[0]);  // AND_Gate
  and a (a_out, and_1_out, and_5_out);
  and c (c_out, and_1_out, and_3_out);
  and b (b_out, and_1_out, and_2_out);
  and d (d_out, and_1_out, and_4_out);
  and and_6 (out_1, a_out, c_out);
  and and_7 (out_2, b_out, d_out);
endmodule

module Nibble_Register (
  input  [3:0] Nibble_In,
  input  Clk,
  output [3:0] Nibble_Out
);

  wire not_1_out, not_2_out, not_3_out, not_4_out;

  // Probe on Nibble_In
  S_R_Flip_Flop s_r_ff_1 (.S(Nibble_In[0]), .R(not_1_out), .clk(Clk), .Q(Nibble_Out[0]));  // open: reset, Qn, preset
  not not_1 (not_1_out, Nibble_In[0]);
  S_R_Flip_Flop s_r_ff_2 (.S(Nibble_In[1]), .R(not_2_out), .clk(Clk), .Q(Nibble_Out[1]));  // open: reset, Qn, preset
  not not_2 (not_2_out, Nibble_In[1]);
  S_R_Flip_Flop s_r_ff_3 (.S(Nibble_In[2]), .R(not_3_out), .clk(Clk), .Q(Nibble_Out[2]));  // open: reset, Qn, preset
  not not_3 (not_3_out, Nibble_In[2]);
  S_R_Flip_Flop s_r_ff_4 (.S(Nibble_In[3]), .R(not_4_out), .clk(Clk), .Q(Nibble_Out[3]));  // open: reset, Qn, preset
  not not_4 (not_4_out, Nibble_In[3]);
  // Probe on Nibble_Out
endmodule
