// Logisim project Assignment_4.circ as structural Verilog: 9 circuits, main circuit main
module Add_1Bit (
  input  A,
  input  B,
  input  C_in,
  output Sum,
  output C_out
);

  wire and_1_out, and_2_out, xor_1_out;

  xor xor_1 (xor_1_out, A, B);
  xor xor_2 (Sum, xor_1_out, C_in);
  and and_1 (and_1_out, xor_1_out, C_in);
  and and_2 (and_2_out, B, A);
  or or_1 (C_out, and_1_out, and_2_out);
endmodule

module ALU (
  input  [3:0] L,
  input  [3:0] R,
  output Zero,
  output Arithmetic_Overflow,
  output [3:0] A_out
);

  wire add_1bit_1_c_out, add_1bit_2_c_out, add_1bit_3_c_out;

  // Probe on L
  // Probe on R
  Add_1Bit add_1bit_1 (.A(L[0]), .B(R[0]), .Sum(A_out[0]), .C_out(add_1bit_1_c_out));  // open: C_in
  Add_1Bit add_1bit_2 (.A(L[1]), .B(R[1]), .C_in(add_1bit_1_c_out), .Sum(A_out[1]), .C_out(add_1bit_2_c_out));
  Add_1Bit add_1bit_3 (.A(L[2]), .B(R[2]), .C_in(add_1bit_2_c_out), .Sum(A_out[2]), .C_out(add_1bit_3_c_out));
  Add_1Bit add_1bit_4 (.A(L[3]), .B(R[3]), .C_in(add_1bit_3_c_out), .Sum(A_out[3]), .C_out(Arithmetic_Overflow));
  nor nor_1 (Zero, A_out[0], A_out[1], A_out[2], A_out[3]);
  // Probe on A_out
endmodule

module Step_Counter (
  input  [1:0] S_in,
  input  Clk,
  output [1:0] S_out
);

  // Probe on S_in
  D_Flip_Flop d_ff_1 (.D(S_in[0]), .clk(Clk), .Q(S_out[0]));  // open: Qn, preset, reset
  D_Flip_Flop d_ff_2 (.D(S_in[1]), .clk(Clk), .Q(S_out[1]));  // open: Qn, preset, reset
  // Probe on S_out
endmodule

module CU (
  input  CU_in,
  input  Clk,
  output [2:0] CU_out
);

  wire [1:0] incr_1_incr_out;

  // Probe on CU_in
  Incr incr_1 (.Incr_in(CU_out[1:0]), .Incr_out(incr_1_incr_out));
  Step_Counter step_counter_1 (.S_in(incr_1_incr_out), .Clk(Clk), .S_out(CU_out[1:0]));
  // Probe on CU_out[1:0]
  // Probe on {CU_in, CU_out[1:0]}

  assign CU_out[2] = CU_in;
endmodule

module Incr (
  input  [1:0] Incr_in,
  output [1:0] Incr_out
);

  wire [3:2] alu_1_a_out;

  // Probe on Incr_in
  ALU alu_1 (.L(4'b0001), .R({2'b00, Incr_in}), .A_out({alu_1_a_out, Incr_out}));  // open: Zero, Arithmetic_Overflow
  // Probe on Incr_out
endmodule

module main (
);

  wire alu_1_arithmetic_overflow, alu_1_zero, and_1_out, and_3_out, and_7_out, and_11_out, and_13_out,
       Clk_out, multiplexer_1_out, not_1_out, not_3_out, not_4_out, or_1_out, or_5_out, or_6_out, or_7_out;
  wire [1:0] and_4_out, and_5_out, and_6_out, cu_1_cu_out, incr_1_incr_out, or_2_out, or_3_out, or_4_out,
       pc_1_pc_out;
  wire [1:1] and_6_out_2, and_9_out, not_2_out;
  wire [3:0] A_out_data_out, alu_1_a_out, and_2_out, and_8_out, and_15_out, IR_data_out, L_data_out,
       R_data_out, ram_4_nibbles_1_ram_0, ram_4_nibbles_1_ram_1, ram_4_nibbles_1_ram_2,
       ram_4_nibbles_1_ram_3, ram_4_nibbles_1_ram_out;
  wire [3:2] or_3_out_2;
  wire [3:3] and_6_out_3, and_10_out, and_12_out, and_14_out, cu_1_cu_out_2;

  Clock Clk (.out(Clk_out));
  Incr incr_1 (.Incr_in(pc_1_pc_out), .Incr_out(incr_1_incr_out));
  not not_1 (not_1_out, and_7_out);
  Multiplexer #(.enable("false")) multiplexer_1 (
    .in0(Clk_out), .in1(not_1_out), .out(multiplexer_1_out), .sel(and_7_out));
  // Probe on pc_1_pc_out
  // Probe on cu_1_cu_out
  PC pc_1 (.PC_in(incr_1_incr_out), .Clk(multiplexer_1_out), .Enable(and_3_out), .PC_out(pc_1_pc_out));
  // Probe on IR_data_out
  and and_1 (and_1_out, not_2_out[1], ~and_13_out);  // AND_Gate
  not not_2 (not_2_out[1], and_3_out);
  assign and_2_out = A_out_data_out & {4{and_14_out[3]}};  // AND_Gate and_2, 4 bits wide
  and and_3 (and_3_out, cu_1_cu_out[0], cu_1_cu_out[1]);
  // Probe on alu_1_zero
  // Probe on A_out_data_out
  or or_1 (or_1_out, and_1_out, and_13_out, not_3_out, and_6_out_2[1]);
  not not_3 (not_3_out, and_14_out[3]);
  assign or_2_out = {2{and_9_out[1]}} | {2{not_2_out[1]}} | or_3_out;  // OR_Gate or_2, 2 bits wide
  assign and_4_out = pc_1_pc_out & ~{2{and_14_out[3]}} & or_2_out;  // AND_Gate and_4, 2 bits wide
  assign and_5_out = {2{and_14_out[3]}} & ~{2{and_6_out_2[1]}} & and_6_out;  // AND_Gate and_5, 2 bits wide
  assign {or_3_out_2, or_3_out} = {4{and_14_out[3]}} | {4{and_12_out[3]}};  // OR_Gate or_3, 4 bits wide
  assign or_4_out = and_4_out | and_5_out;  // OR_Gate or_4, 2 bits wide
  assign {and_6_out_3[3], and_6_out_2[1], and_6_out} = IR_data_out & {4{cu_1_cu_out_2[3]}};  // AND_Gate and_6, 4 bits wide
  // Probe on alu_1_arithmetic_overflow
  and and_7 (and_7_out, and_8_out[0], and_8_out[1], and_8_out[2], and_8_out[3]);
  assign and_8_out = {4{and_10_out[3]}} & ~IR_data_out;  // AND_Gate and_8, 4 bits wide
  and and_9 (and_9_out[1], ~cu_1_cu_out_2[3], ~cu_1_cu_out[1], ~cu_1_cu_out[0]);  // AND_Gate
  // Probe on ram_4_nibbles_1_ram_0
  // Probe on ram_4_nibbles_1_ram_1
  // Probe on ram_4_nibbles_1_ram_2
  // Probe on ram_4_nibbles_1_ram_3
  and and_10 (and_10_out[3], ~cu_1_cu_out_2[3], ~cu_1_cu_out[1], cu_1_cu_out[0]);  // AND_Gate
  and and_11 (and_11_out, ~cu_1_cu_out_2[3], cu_1_cu_out[1], ~cu_1_cu_out[0]);  // AND_Gate
  CU cu_1 (.CU_in(IR_data_out[3]), .Clk(multiplexer_1_out), .CU_out({cu_1_cu_out_2[3], cu_1_cu_out}));
  RAM_4_Nibbles ram_4_nibbles_1 (
    .Data(and_2_out), .Read_Write(or_1_out), .Address(or_4_out), .Clk(multiplexer_1_out),
    .RAM_out(ram_4_nibbles_1_ram_out), .RAM_0(ram_4_nibbles_1_ram_0), .RAM_1(ram_4_nibbles_1_ram_1),
    .RAM_2(ram_4_nibbles_1_ram_2), .RAM_3(ram_4_nibbles_1_ram_3));
  or or_5 (or_5_out, and_12_out[3], and_14_out[3], and_10_out[3]);
  and and_12 (and_12_out[3], cu_1_cu_out_2[3], ~cu_1_cu_out[1], cu_1_cu_out[0]);  // AND_Gate
  and and_13 (and_13_out, cu_1_cu_out_2[3], cu_1_cu_out[1], ~cu_1_cu_out[0]);  // AND_Gate
  and and_14 (and_14_out[3], cu_1_cu_out_2[3], cu_1_cu_out[1], cu_1_cu_out[0]);
  Nibble IR (
    .Data(ram_4_nibbles_1_ram_out), .Read_Write(or_5_out), .Clk(multiplexer_1_out), .Enable(not_2_out[1]),
    .Data_out(IR_data_out));
  assign and_15_out = IR_data_out & {4{and_10_out[3]}};  // AND_Gate and_15, 4 bits wide
  or or_6 (or_6_out, and_11_out, ~and_10_out[3]);  // OR_Gate
  or or_7 (or_7_out, ~and_11_out, and_10_out[3]);  // OR_Gate
  Nibble L (
    .Data(and_15_out), .Read_Write(or_6_out), .Clk(multiplexer_1_out), .Enable(or_7_out),
    .Data_out(L_data_out));
  Nibble R (
    .Data(and_15_out), .Read_Write(or_6_out), .Clk(multiplexer_1_out), .Enable(or_7_out),
    .Data_out(R_data_out));
  ALU alu_1 (
    .L(L_data_out), .R(R_data_out), .Zero(alu_1_zero), .Arithmetic_Overflow(alu_1_arithmetic_overflow),
    .A_out(alu_1_a_out));
  not not_4 (not_4_out, and_11_out);
  Nibble A_out (
    .Data(alu_1_a_out), .Read_Write(not_4_out), .Clk(multiplexer_1_out), .Enable(and_11_out),
    .Data_out(A_out_data_out));

  // Notes on the sheet:
  //   Le, Nhat Hung - 260793376
  //   To initilize an instruction in RAM:
  //   Right-click RAM_4_Nibbles > View RAM_4_Nibbles > Right-click a Nibble > View Nibble > Use the hand/finger icon and directly click on THE FLIP-FLOPS to set an instruction as desired.
  //   Similarly set instructions in other Nibbles in RAM.
  //   To run circuit, just starting clicking the clock.
endmodule

module Nibble (
  input  [3:0] Data,
  input  Read_Write,
  input  Clk,
  input  Enable,
  output [3:0] Data_out
);

  wire and_1_out, and_2_out, and_3_out, and_4_out, and_5_out, and_6_out, and_7_out, and_8_out, and_9_out,
       not_1_out, not_2_out, not_3_out, not_4_out, not_5_out;

  // Probe on Data
  not not_1 (not_1_out, Data[3]);
  not not_2 (not_2_out, Data[2]);
  not not_3 (not_3_out, Data[1]);
  not not_4 (not_4_out, Data[0]);
  and and_1 (and_1_out, Enable, Data[3]);
  and and_2 (and_2_out, Enable, not_1_out);
  and and_3 (and_3_out, Enable, Data[2]);
  and and_4 (and_4_out, Enable, not_2_out);
  and and_5 (and_5_out, Enable, Data[1]);
  and and_6 (and_6_out, Enable, not_3_out);
  and and_7 (and_7_out, Enable, Data[0]);
  and and_8 (and_8_out, Enable, not_4_out);
  not not_5 (not_5_out, Read_Write);
  and and_9 (and_9_out, not_5_out, Clk);
  S_R_Flip_Flop s_r_ff_1 (.S(and_1_out), .R(and_2_out), .clk(and_9_out), .Q(Data_out[3]));  // open: reset, Qn, preset
  S_R_Flip_Flop s_r_ff_2 (.S(and_3_out), .R(and_4_out), .clk(and_9_out), .Q(Data_out[2]));  // open: reset, Qn, preset
  S_R_Flip_Flop s_r_ff_3 (.S(and_5_out), .R(and_6_out), .clk(and_9_out), .Q(Data_out[1]));  // open: reset, Qn, preset
  S_R_Flip_Flop s_r_ff_4 (.S(and_7_out), .R(and_8_out), .clk(and_9_out), .Q(Data_out[0]));  // open: reset, Qn, preset
  // Probe on Data_out

  // Notes on the sheet:
  //   When Read_Write = 1 performs read, otherwise performs write
endmodule

module RAM_4_Nibbles (
  input  [3:0] Data,
  input  Read_Write,
  input  [1:0] Address,
  input  Clk,
  output [3:0] RAM_out,
  output [3:0] RAM_0,
  output [3:0] RAM_1,
  output [3:0] RAM_2,
  output [3:0] RAM_3
);

  wire and_1_out, and_2_out, and_3_out, and_4_out, and_5_out, and_6_out, and_7_out, and_8_out, and_9_out,
       and_10_out, and_11_out, and_12_out, and_13_out, and_14_out, and_15_out, and_16_out, and_17_out,
       and_18_out, and_19_out, and_20_out, not_1_out, not_2_out, not_3_out, not_4_out, or_5_out, or_6_out,
       or_7_out, or_8_out, or_9_out, or_10_out, or_11_out, or_12_out;

  not not_1 (not_1_out, Address[1]);
  and and_1 (and_1_out, not_1_out, not_2_out);
  not not_2 (not_2_out, Address[0]);
  not not_3 (not_3_out, Address[1]);
  and and_2 (and_2_out, not_3_out, Address[0]);
  and and_3 (and_3_out, Address[1], not_4_out);
  not not_4 (not_4_out, Address[0]);
  and and_4 (and_4_out, Address[0], Address[1]);
  Nibble nibble_1 (.Data(Data), .Read_Write(Read_Write), .Clk(Clk), .Enable(and_1_out), .Data_out(RAM_0));
  Nibble nibble_2 (.Data(Data), .Read_Write(Read_Write), .Clk(Clk), .Enable(and_2_out), .Data_out(RAM_1));
  Nibble nibble_3 (.Data(Data), .Read_Write(Read_Write), .Clk(Clk), .Enable(and_3_out), .Data_out(RAM_2));
  Nibble nibble_4 (.Data(Data), .Read_Write(Read_Write), .Clk(Clk), .Enable(and_4_out), .Data_out(RAM_3));
  // Probe on Address
  and and_5 (and_5_out, and_1_out, RAM_0[0]);
  and and_6 (and_6_out, and_1_out, RAM_0[1]);
  and and_7 (and_7_out, and_1_out, RAM_0[2]);
  and and_8 (and_8_out, and_1_out, RAM_0[3]);
  and and_9 (and_9_out, and_2_out, RAM_1[0]);
  and and_10 (and_10_out, and_2_out, RAM_1[1]);
  and and_11 (and_11_out, and_2_out, RAM_1[2]);
  and and_12 (and_12_out, and_2_out, RAM_1[3]);
  and and_13 (and_13_out, and_3_out, RAM_2[0]);
  and and_14 (and_14_out, and_3_out, RAM_2[1]);
  and and_15 (and_15_out, and_3_out, RAM_2[2]);
  and and_16 (and_16_out, and_3_out, RAM_2[3]);
  and and_17 (and_17_out, and_4_out, RAM_3[0]);
  and and_18 (and_18_out, and_4_out, RAM_3[1]);
  and and_19 (and_19_out, and_4_out, RAM_3[2]);
  and and_20 (and_20_out, and_4_out, RAM_3[3]);
  // Probe on RAM_out
  or or_1 (RAM_out[0], and_5_out, or_11_out);
  or or_2 (RAM_out[1], and_6_out, or_5_out);
  or or_3 (RAM_out[2], and_7_out, or_6_out);
  or or_4 (RAM_out[3], and_8_out, or_7_out);
  or or_5 (or_5_out, and_10_out, or_8_out);
  or or_6 (or_6_out, and_11_out, or_9_out);
  or or_7 (or_7_out, and_12_out, or_10_out);
  or or_8 (or_8_out, and_14_out, and_18_out);
  or or_9 (or_9_out, and_15_out, and_19_out);
  or or_10 (or_10_out, and_16_out, and_20_out);
  or or_11 (or_11_out, and_9_out, or_12_out);
  or or_12 (or_12_out, and_13_out, and_17_out);

  // Notes on the sheet:
  //   When Read_Write = 1 performs read, otherwise performs write
endmodule

module PC (
  input  [1:0] PC_in,
  input  Clk,
  input  Enable,
  output [1:0] PC_out
);

  wire and_1_out, and_2_out, and_3_out, and_4_out, not_1_out, not_2_out;

  // Probe on PC_in
  not not_1 (not_1_out, PC_in[1]);
  not not_2 (not_2_out, PC_in[0]);
  and and_1 (and_1_out, Enable, PC_in[1]);
  and and_2 (and_2_out, Enable, not_1_out);
  and and_3 (and_3_out, Enable, PC_in[0]);
  and and_4 (and_4_out, Enable, not_2_out);
  S_R_Flip_Flop s_r_ff_1 (.S(and_1_out), .R(and_2_out), .clk(Clk), .Q(PC_out[1]));  // open: reset, Qn, preset
  S_R_Flip_Flop s_r_ff_2 (.S(and_3_out), .R(and_4_out), .clk(Clk), .Q(PC_out[0]));  // open: reset, Qn, preset
  // Probe on PC_out
endmodule
