// Logisim project RAM_16_Nibbles_Read_Write.circ as structural Verilog: 2 circuits, main circuit RAM_16_Nibbles
// Clk
module RAM_16_Nibbles (
  input  [3:0] Data,
  input  [3:0] Address,
  input  Read_Write,
  output [3:0] RAM_OUT,
  output out_5,
  output out_6,
  output out_7,
  output out_8,
  output out_9,
  output out_10,
  output out_11,
  output out_12,
  output out_13,
  output out_14,
  output out_15,
  output out_16,
  output out_17,
  output out_18,
  output out_19,
  output out_20
);

  wire and_1_out, and_2_out, and_3_out, and_4_out, and_5_out, and_6_out, and_7_out, and_8_out, and_9_out,
       and_10_out, and_11_out, and_12_out, and_13_out, and_14_out, and_15_out, and_16_out, and_17_out,
       and_18_out, and_19_out, and_20_out, and_21_out, and_22_out, and_23_out, and_24_out, and_25_out,
       and_26_out, and_27_out, and_28_out, and_29_out, and_30_out, and_31_out, and_32_out, and_33_out,
       and_34_out, and_35_out, and_36_out, and_37_out, and_38_out, and_39_out, and_40_out, and_41_out,
       and_42_out, and_43_out, and_44_out, and_45_out, and_46_out, and_47_out, and_48_out, and_49_out,
       and_50_out, and_51_out, and_52_out, and_53_out, and_54_out, and_55_out, and_56_out, and_57_out,
       and_58_out, and_59_out, and_60_out, and_61_out, and_62_out, and_63_out, and_64_out, and_65_out,
       and_66_out, and_67_out, and_68_out, and_69_out, and_70_out, and_71_out, and_72_out, and_73_out,
       and_74_out, and_75_out, and_76_out, and_77_out, and_78_out, and_79_out, and_80_out, Clk_out,
       not_1_out, not_2_out, not_3_out, not_4_out, not_5_out, not_6_out, not_7_out, not_8_out, not_9_out,
       not_10_out, not_11_out, not_12_out, not_13_out, not_14_out, not_15_out, not_16_out, not_17_out,
       not_18_out, not_19_out, not_20_out, not_21_out, not_22_out, not_23_out, not_24_out, not_25_out,
       not_26_out, not_27_out, not_28_out, not_29_out, not_30_out, not_31_out, not_32_out, not_33_out,
       not_34_out, not_35_out, not_36_out, not_37_out, not_38_out, not_39_out, not_40_out, not_41_out,
       not_42_out, not_43_out, not_44_out, not_45_out, not_46_out, not_47_out, not_48_out, s_r_ff_1_q,
       s_r_ff_2_q, s_r_ff_3_q, s_r_ff_4_q, s_r_ff_5_q, s_r_ff_6_q, s_r_ff_7_q, s_r_ff_8_q, s_r_ff_9_q,
       s_r_ff_10_q, s_r_ff_11_q, s_r_ff_12_q, s_r_ff_13_q, s_r_ff_14_q, s_r_ff_15_q, s_r_ff_16_q;
  wire [3:0] addr0000_nibble_out, addr0001_nibble_out, addr0010_nibble_out, addr0011_nibble_out,
       addr0100_nibble_out, addr0101_nibble_out, addr0110_nibble_out, addr0111_nibble_out,
       addr1000_nibble_out, addr1001_nibble_out, addr1010_nibble_out, addr1011_nibble_out,
       addr1100_nibble_out, addr1101_nibble_out, addr1110_nibble_out, addr1111_nibble_out;

  Clock Clk (.out(Clk_out));
  // Probe on Data
  // Probe on Address
  not not_1 (not_1_out, Address[0]);
  not not_2 (not_2_out, Address[1]);
  and and_1 (and_1_out, not_1_out, not_2_out, not_3_out, not_4_out);
  not not_3 (not_3_out, Address[2]);
  not not_4 (not_4_out, Address[3]);
  not not_5 (not_5_out, Address[1]);
  and and_2 (and_2_out, Address[0], not_5_out, not_6_out, not_7_out);
  not not_6 (not_6_out, Address[2]);
  not not_7 (not_7_out, Address[3]);
  not not_8 (not_8_out, Address[0]);
  and and_3 (and_3_out, not_8_out, Address[1], not_9_out, not_10_out);
  not not_9 (not_9_out, Address[2]);
  not not_10 (not_10_out, Address[3]);
  and and_4 (and_4_out, Address[0], Address[1], not_11_out, not_12_out);
  not not_11 (not_11_out, Address[2]);
  not not_12 (not_12_out, Address[3]);
  not not_13 (not_13_out, Address[0]);
  not not_14 (not_14_out, Address[1]);
  and and_5 (and_5_out, not_13_out, not_14_out, Address[2], not_15_out);
  not not_15 (not_15_out, Address[3]);
  not not_16 (not_16_out, Address[1]);
  and and_6 (and_6_out, Address[0], not_16_out, Address[2], not_17_out);
  not not_17 (not_17_out, Address[3]);
  not not_18 (not_18_out, Address[0]);
  and and_7 (and_7_out, not_18_out, Address[1], Address[2], not_19_out);
  not not_19 (not_19_out, Address[3]);
  and and_8 (and_8_out, Address[0], Address[1], Address[2], not_20_out);
  not not_20 (not_20_out, Address[3]);
  not not_21 (not_21_out, Address[0]);
  not not_22 (not_22_out, Address[1]);
  and and_9 (and_9_out, not_21_out, not_22_out, not_23_out, Address[3]);
  not not_23 (not_23_out, Address[2]);
  not not_24 (not_24_out, Address[1]);
  and and_10 (and_10_out, Address[0], not_24_out, not_25_out, Address[3]);
  not not_25 (not_25_out, Address[2]);
  not not_26 (not_26_out, Address[0]);
  and and_11 (and_11_out, not_26_out, Address[1], not_27_out, Address[3]);
  not not_27 (not_27_out, Address[2]);
  and and_12 (and_12_out, Address[0], Address[1], not_28_out, Address[3]);
  not not_28 (not_28_out, Address[2]);
  not not_29 (not_29_out, Address[0]);
  not not_30 (not_30_out, Address[1]);
  and and_13 (and_13_out, not_29_out, not_30_out, Address[2], Address[3]);
  not not_31 (not_31_out, Address[1]);
  and and_14 (and_14_out, Address[0], not_31_out, Address[2], Address[3]);
  not not_32 (not_32_out, Address[0]);
  and and_15 (and_15_out, not_32_out, Address[1], Address[2], Address[3]);
  and and_16 (and_16_out, Address[0], Address[1], Address[2], Address[3]);
  not not_33 (not_33_out, and_1_out);
  not not_34 (not_34_out, and_2_out);
  not not_35 (not_35_out, and_3_out);
  not not_36 (not_36_out, and_11_out);
  S_R_Flip_Flop s_r_ff_1 (
    .S(and_1_out), .R(not_33_out), .clk(Clk_out), .Q(s_r_ff_1_q), .Qn(out_5));  // open: reset, preset
  S_R_Flip_Flop s_r_ff_2 (
    .S(and_2_out), .R(not_34_out), .clk(Clk_out), .Q(s_r_ff_2_q), .Qn(out_6));  // open: reset, preset
  S_R_Flip_Flop s_r_ff_3 (
    .S(and_3_out), .R(not_35_out), .clk(Clk_out), .Q(s_r_ff_3_q), .Qn(out_7));  // open: reset, preset
  S_R_Flip_Flop s_r_ff_4 (
    .S(and_4_out), .R(not_37_out), .clk(Clk_out), .Q(s_r_ff_4_q), .Qn(out_8));  // open: reset, preset
  not not_37 (not_37_out, and_4_out);
  S_R_Flip_Flop s_r_ff_5 (
    .S(and_5_out), .R(not_38_out), .clk(Clk_out), .Q(s_r_ff_5_q), .Qn(out_9));  // open: reset, preset
  not not_38 (not_38_out, and_5_out);
  S_R_Flip_Flop s_r_ff_6 (
    .S(and_6_out), .R(not_39_out), .clk(Clk_out), .Q(s_r_ff_6_q), .Qn(out_10));  // open: reset, preset
  not not_39 (not_39_out, and_6_out);
  S_R_Flip_Flop s_r_ff_7 (
    .S(and_7_out), .R(not_40_out), .clk(Clk_out), .Q(s_r_ff_7_q), .Qn(out_11));  // open: reset, preset
  not not_40 (not_40_out, and_7_out);
  S_R_Flip_Flop s_r_ff_8 (
    .S(and_8_out), .R(not_41_out), .clk(Clk_out), .Q(s_r_ff_8_q), .Qn(out_12));  // open: reset, preset
  not not_41 (not_41_out, and_8_out);
  S_R_Flip_Flop s_r_ff_9 (
    .S(and_9_out), .R(not_42_out), .clk(Clk_out), .Q(s_r_ff_9_q), .Qn(out_13));  // open: reset, preset
  not not_42 (not_42_out, and_9_out);
  S_R_Flip_Flop s_r_ff_10 (
    .S(and_10_out), .R(not_43_out), .clk(Clk_out), .Q(s_r_ff_10_q), .Qn(out_14));  // open: reset, preset
  not not_43 (not_43_out, and_10_out);
  S_R_Flip_Flop s_r_ff_11 (
    .S(and_11_out), .R(not_36_out), .clk(Clk_out), .Q(s_r_ff_11_q), .Qn(out_15));  // open: reset, preset
  S_R_Flip_Flop s_r_ff_12 (
    .S(and_12_out), .R(not_44_out), .clk(Clk_out), .Q(s_r_ff_12_q), .Qn(out_16));  // open: reset, preset
  not not_44 (not_44_out, and_12_out);
  S_R_Flip_Flop s_r_ff_13 (
    .S(and_13_out), .R(not_45_out), .clk(Clk_out), .Q(s_r_ff_13_q), .Qn(out_17));  // open: reset, preset
  not not_45 (not_45_out, and_13_out);
  S_R_Flip_Flop s_r_ff_14 (
    .S(and_14_out), .R(not_46_out), .clk(Clk_out), .Q(s_r_ff_14_q), .Qn(out_18));  // open: reset, preset
  not not_46 (not_46_out, and_14_out);
  S_R_Flip_Flop s_r_ff_15 (
    .S(and_15_out), .R(not_47_out), .clk(Clk_out), .Q(s_r_ff_15_q), .Qn(out_19));  // open: reset, preset
  not not_47 (not_47_out, and_15_out);
  S_R_Flip_Flop s_r_ff_16 (
    .S(and_16_out), .R(not_48_out), .clk(Clk_out), .Q(s_r_ff_16_q), .Qn(out_20));  // open: reset, preset
  not not_48 (not_48_out, and_16_out);
  Nibble addr0000 (
    .Data(Data), .Read_Write(Read_Write), .Enable(and_1_out), .CLK(Clk_out), .Nibble_Out(addr0000_nibble_out));
  Nibble addr0001 (
    .Data(Data), .Read_Write(Read_Write), .Enable(and_2_out), .CLK(Clk_out), .Nibble_Out(addr0001_nibble_out));
  Nibble addr0010 (
    .Data(Data), .Read_Write(Read_Write), .Enable(and_3_out), .CLK(Clk_out), .Nibble_Out(addr0010_nibble_out));
  Nibble addr0011 (
    .Data(Data), .Read_Write(Read_Write), .Enable(and_4_out), .CLK(Clk_out), .Nibble_Out(addr0011_nibble_out));
  Nibble addr0100 (
    .Data(Data), .Read_Write(Read_Write), .Enable(and_5_out), .CLK(Clk_out), .Nibble_Out(addr0100_nibble_out));
  Nibble addr0101 (
    .Data(Data), .Read_Write(Read_Write), .Enable(and_6_out), .CLK(Clk_out), .Nibble_Out(addr0101_nibble_out));
  Nibble addr0110 (
    .Data(Data), .Read_Write(Read_Write), .Enable(and_7_out), .CLK(Clk_out), .Nibble_Out(addr0110_nibble_out));
  Nibble addr0111 (
    .Data(Data), .Read_Write(Read_Write), .Enable(and_8_out), .CLK(Clk_out), .Nibble_Out(addr0111_nibble_out));
  Nibble addr1000 (
    .Data(Data), .Read_Write(Read_Write), .Enable(and_9_out), .CLK(Clk_out), .Nibble_Out(addr1000_nibble_out));
  Nibble addr1001 (
    .Data(Data), .Read_Write(Read_Write), .Enable(and_10_out), .CLK(Clk_out), .Nibble_Out(addr1001_nibble_out));
  Nibble addr1010 (
    .Data(Data), .Read_Write(Read_Write), .Enable(and_11_out), .CLK(Clk_out), .Nibble_Out(addr1010_nibble_out));
  Nibble addr1011 (
    .Data(Data), .Read_Write(Read_Write), .Enable(and_12_out), .CLK(Clk_out), .Nibble_Out(addr1011_nibble_out));
  Nibble addr1100 (
    .Data(Data), .Read_Write(Read_Write), .Enable(and_13_out), .CLK(Clk_out), .Nibble_Out(addr1100_nibble_out));
  Nibble addr1101 (
    .Data(Data), .Read_Write(Read_Write), .Enable(and_14_out), .CLK(Clk_out), .Nibble_Out(addr1101_nibble_out));
  Nibble addr1110 (
    .Data(Data), .Read_Write(Read_Write), .Enable(and_15_out), .CLK(Clk_out), .Nibble_Out(addr1110_nibble_out));
  Nibble addr1111 (
    .Data(Data), .Read_Write(Read_Write), .Enable(and_16_out), .CLK(Clk_out), .Nibble_Out(addr1111_nibble_out));
  and and_17 (and_17_out, addr0000_nibble_out[0], s_r_ff_1_q);
  and and_18 (and_18_out, addr0000_nibble_out[1], s_r_ff_1_q);
  and and_19 (and_19_out, addr0000_nibble_out[2], s_r_ff_1_q);
  and and_20 (and_20_out, addr0000_nibble_out[3], s_r_ff_1_q);
  and and_21 (and_21_out, addr0001_nibble_out[0], s_r_ff_2_q);
  and and_22 (and_22_out, addr0001_nibble_out[1], s_r_ff_2_q);
  and and_23 (and_23_out, addr0001_nibble_out[2], s_r_ff_2_q);
  and and_24 (and_24_out, addr0001_nibble_out[3], s_r_ff_2_q);
  and and_25 (and_25_out, addr0010_nibble_out[0], s_r_ff_3_q);
  and and_26 (and_26_out, addr0010_nibble_out[1], s_r_ff_3_q);
  and and_27 (and_27_out, addr0010_nibble_out[2], s_r_ff_3_q);
  and and_28 (and_28_out, addr0010_nibble_out[3], s_r_ff_3_q);
  and and_29 (and_29_out, addr0011_nibble_out[0], s_r_ff_4_q);
  and and_30 (and_30_out, addr0011_nibble_out[1], s_r_ff_4_q);
  and and_31 (and_31_out, addr0011_nibble_out[2], s_r_ff_4_q);
  and and_32 (and_32_out, addr0011_nibble_out[3], s_r_ff_4_q);
  and and_33 (and_33_out, addr0100_nibble_out[0], s_r_ff_5_q);
  and and_34 (and_34_out, addr0100_nibble_out[1], s_r_ff_5_q);
  and and_35 (and_35_out, addr0100_nibble_out[2], s_r_ff_5_q);
  and and_36 (and_36_out, addr0100_nibble_out[3], s_r_ff_5_q);
  and and_37 (and_37_out, addr0101_nibble_out[0], s_r_ff_6_q);
  and and_38 (and_38_out, addr0101_nibble_out[1], s_r_ff_6_q);
  and and_39 (and_39_out, addr0101_nibble_out[2], s_r_ff_6_q);
  and and_40 (and_40_out, addr0101_nibble_out[3], s_r_ff_6_q);
  and and_41 (and_41_out, addr0110_nibble_out[0], s_r_ff_7_q);
  and and_42 (and_42_out, addr0110_nibble_out[1], s_r_ff_7_q);
  and and_43 (and_43_out, addr0110_nibble_out[2], s_r_ff_7_q);
  and and_44 (and_44_out, addr0110_nibble_out[3], s_r_ff_7_q);
  and and_45 (and_45_out, addr0111_nibble_out[0], s_r_ff_8_q);
  and and_46 (and_46_out, addr0111_nibble_out[1], s_r_ff_8_q);
  and and_47 (and_47_out, addr0111_nibble_out[2], s_r_ff_8_q);
  and and_48 (and_48_out, addr0111_nibble_out[3], s_r_ff_8_q);
  and and_49 (and_49_out, addr1000_nibble_out[0], s_r_ff_9_q);
  and and_50 (and_50_out, addr1000_nibble_out[1], s_r_ff_9_q);
  and and_51 (and_51_out, addr1000_nibble_out[2], s_r_ff_9_q);
  and and_52 (and_52_out, addr1000_nibble_out[3], s_r_ff_9_q);
  and and_53 (and_53_out, addr1001_nibble_out[0], s_r_ff_10_q);
  and and_54 (and_54_out, addr1001_nibble_out[1], s_r_ff_10_q);
  and and_55 (and_55_out, addr1001_nibble_out[2], s_r_ff_10_q);
  and and_56 (and_56_out, addr1001_nibble_out[3], s_r_ff_10_q);
  and and_57 (and_57_out, addr1010_nibble_out[0], s_r_ff_11_q);
  and and_58 (and_58_out, addr1010_nibble_out[1], s_r_ff_11_q);
  and and_59 (and_59_out, addr1010_nibble_out[2], s_r_ff_11_q);
  and and_60 (and_60_out, addr1010_nibble_out[3], s_r_ff_11_q);
  and and_61 (and_61_out, addr1011_nibble_out[0], s_r_ff_12_q);
  and and_62 (and_62_out, addr1011_nibble_out[1], s_r_ff_12_q);
  and and_63 (and_63_out, addr1011_nibble_out[2], s_r_ff_12_q);
  and and_64 (and_64_out, addr1011_nibble_out[3], s_r_ff_12_q);
  and and_65 (and_65_out, addr1100_nibble_out[0], s_r_ff_13_q);
  and and_66 (and_66_out, addr1100_nibble_out[1], s_r_ff_13_q);
  and and_67 (and_67_out, addr1100_nibble_out[2], s_r_ff_13_q);
  and and_68 (and_68_out, addr1100_nibble_out[3], s_r_ff_13_q);
  and and_69 (and_69_out, addr1101_nibble_out[0], s_r_ff_14_q);
  and and_70 (and_70_out, addr1101_nibble_out[1], s_r_ff_14_q);
  and and_71 (and_71_out, addr1101_nibble_out[2], s_r_ff_14_q);
  and and_72 (and_72_out, addr1101_nibble_out[3], s_r_ff_14_q);
  and and_73 (and_73_out, addr1110_nibble_out[0], s_r_ff_15_q);
  and and_74 (and_74_out, addr1110_nibble_out[1], s_r_ff_15_q);
  and and_75 (and_75_out, addr1110_nibble_out[2], s_r_ff_15_q);
  and and_76 (and_76_out, addr1110_nibble_out[3], s_r_ff_15_q);
  and and_77 (and_77_out, addr1111_nibble_out[0], s_r_ff_16_q);
  and and_78 (and_78_out, addr1111_nibble_out[1], s_r_ff_16_q);
  and and_79 (and_79_out, addr1111_nibble_out[2], s_r_ff_16_q);
  and and_80 (and_80_out, addr1111_nibble_out[3], s_r_ff_16_q);
  or or_1 (RAM_OUT[3], and_20_out, and_24_out, and_28_out, and_32_out, and_36_out, and_40_out, and_44_out, and_48_out, and_52_out, and_56_out, and_60_out, and_64_out, and_68_out, and_72_out, and_76_out, and_80_out);
  or or_2 (RAM_OUT[2], and_19_out, and_23_out, and_27_out, and_31_out, and_35_out, and_39_out, and_43_out, and_47_out, and_51_out, and_55_out, and_59_out, and_63_out, and_67_out, and_71_out, and_75_out, and_79_out);
  or or_3 (RAM_OUT[1], and_18_out, and_22_out, and_26_out, and_30_out, and_34_out, and_38_out, and_42_out, and_46_out, and_50_out, and_54_out, and_58_out, and_62_out, and_66_out, and_70_out, and_74_out, and_78_out);
  or or_4 (RAM_OUT[0], and_17_out, and_21_out, and_25_out, and_29_out, and_33_out, and_37_out, and_41_out, and_45_out, and_49_out, and_53_out, and_57_out, and_61_out, and_65_out, and_69_out, and_73_out, and_77_out);
  // Probe on RAM_OUT

  // Notes on the sheet:
  //   Eunbee Jang (260 658 722)
  //   When Read_Write = 1 performs read, otherwise performs write
endmodule

module Nibble (
  input  [3:0] Data,
  input  Read_Write,
  input  Enable,
  input  CLK,
  output [3:0] Nibble_Out
);

  wire and_1_out, d_ff_1_q, d_ff_2_q, d_ff_3_q, d_ff_4_q, nor_1_out, or_1_out;

  // Probe on Data
  nor nor_1 (nor_1_out, Read_Write, Read_Write);
  and and_1 (and_1_out, nor_1_out, CLK, Enable);
  D_Flip_Flop d_ff_1 (.D(Data[0]), .clk(and_1_out), .Q(d_ff_1_q));  // open: Qn, preset, reset
  D_Flip_Flop d_ff_2 (.D(Data[1]), .clk(and_1_out), .Q(d_ff_2_q));  // open: Qn, preset, reset
  D_Flip_Flop d_ff_3 (.D(Data[2]), .clk(and_1_out), .Q(d_ff_3_q));  // open: Qn, preset, reset
  D_Flip_Flop d_ff_4 (.D(Data[3]), .clk(and_1_out), .Q(d_ff_4_q));  // open: Qn, preset, reset
  or or_1 (or_1_out, Read_Write, nor_1_out);
  and and_2 (Nibble_Out[0], or_1_out, d_ff_1_q);
  and and_3 (Nibble_Out[1], or_1_out, d_ff_2_q);
  and and_4 (Nibble_Out[2], or_1_out, d_ff_3_q);
  and and_5 (Nibble_Out[3], or_1_out, d_ff_4_q);
  // Probe on Nibble_Out

  // Notes on the sheet:
  //   Eunbee Jang (260 658 722)
  //   When Read_Write = 1 performs read, otherwise performs write
  //   MAKE SURE THAT YOU OPEN THIS PROJECT IN "LOGISIM-EVOLUTION"
  //   YOU CAN FIND "LOGISIM-EVOLUTION" PROGRAM IN THE ASSIGNMENT'S FOLDER
  //   DO NOT USE "LOGISIM" VERSION TO SOLVE THIS ASSIGNMENT!
endmodule
