// Logisim project ass8 (1).circ as structural Verilog: 9 circuits, main circuit Main
module Main (
  output [3:0] out_1,
  output [1:0] out_2,
  output [3:0] out_3,
  output [3:0] out_4,
  output [3:0] out_5,
  output [3:0] out_6,
  output [3:0] out_7,
  output [1:0] out_8,
  output [1:0] out_9,
  output [1:0] out_10,
  output [3:0] out_11,
  output [1:0] out_12,
  output [3:0] out_13,
  output out_14,
  output out_15
);

  wire and_1_out, and_11_out, and_12_out, and_15_out, and_16_out, and_18_out, Clk_out, not_1_out, not_2_out,
       or_2_out;
  wire [1:0] and_2_out, and_13_out;
  wire [2:0] and_10_out;
  wire [3:0] alu_1_aout;

  Clock Clk (.out(Clk_out));
  and and_1 (and_1_out, ~and_11_out, and_18_out);  // AND_Gate
  ALU alu_1 (
    .A({1'b0, and_10_out}), .B({1'b0, and_10_out}), .AddSub(and_12_out), .Aout(alu_1_aout), .Zero(out_14),
    .Overflow(out_15));
  PC pc_1 (.Data(out_8), .Enabled(and_1_out), .Clock(Clk_out), .DataOut(out_9));
  Inc inc_1 (.DataIn(out_9), .DataOut(out_8));  // open: Overlfow
  and and_2 (and_2_out[0], out_9[0], and_15_out);
  and and_3 (and_2_out[1], out_9[1], and_15_out);
  Aout aout_1 (.DataIn(alu_1_aout), .Clk(Clk_out), .Enabled(and_12_out), .DataOut(out_13));
  and and_4 (out_1[0], out_11[3], out_13[0]);
  and and_5 (out_1[1], out_11[3], out_13[1]);
  and and_6 (out_1[2], out_11[3], out_13[2]);
  and and_7 (out_1[3], out_11[3], out_13[3]);
  not not_1 (not_1_out, out_11[3]);
  assign out_2 = and_2_out | and_13_out;  // OR_Gate or_1, 2 bits wide
  Nibbles_RAM nibbles_ram_1 (
    .Data(out_1), .Read_Write(not_1_out), .Address(out_2), .Clk(Clk_out), .RAM_OUT(out_3), .out_6(out_4),
    .out_7(out_5), .out_8(out_6), .out_9(out_7));
  IR ir_1 (.Data(out_3), .Enabled(and_15_out), .Clock(Clk_out), .DataOut(out_11));
  and and_8 (and_10_out[2], out_11[2], and_12_out);
  and and_9 (and_10_out[1], out_11[1], and_12_out);
  and and_10 (and_10_out[0], out_11[0], and_12_out);
  and and_11 (and_11_out, ~out_11[0], ~out_11[1], and_16_out, ~out_11[2], ~out_11[3]);  // AND_Gate
  or or_2 (or_2_out, out_11[0], out_11[1], out_11[2]);
  and and_12 (and_12_out, or_2_out, ~out_11[3]);  // AND_Gate
  and and_13 (and_13_out[0], out_11[1], ~out_11[2], out_11[3]);  // AND_Gate
  and and_14 (and_13_out[1], out_11[0], ~out_11[2], out_11[3]);  // AND_Gate
  not not_2 (not_2_out, and_11_out);
  and and_15 (and_15_out, ~out_12[0], ~out_12[1]);  // AND_Gate
  and and_16 (and_16_out, out_12[0], ~out_12[1]);  // AND_Gate
  // AND_Gate and_17 has open pins: in0=out_12[0], in1=out_12[1], out=open
  and and_18 (and_18_out, out_12[0], out_12[1]);
  Steps steps_1 (.Data(out_10), .Enable(not_2_out), .Clk(Clk_out), .Dataout(out_12));
  Inc inc_2 (.DataIn(out_12), .DataOut(out_10));  // open: Overlfow
endmodule

module Nibble (
  input  [3:0] in_1,
  input  Read_Write,
  input  Clk,
  input  Enable,
  output [3:0] Nibble_Out
);

  wire and_1_out, and_2_out, and_3_out, and_4_out, and_5_out, and_6_out, and_7_out, and_8_out, and_9_out,
       not_1_out, not_2_out, not_3_out, not_4_out, not_5_out;

  // Probe on in_1
  and and_1 (and_1_out, Enable, in_1[3]);
  and and_2 (and_2_out, Enable, in_1[3]);
  and and_3 (and_3_out, Enable, in_1[2]);
  and and_4 (and_4_out, Enable, in_1[2]);
  and and_5 (and_5_out, Enable, in_1[1]);
  and and_6 (and_6_out, Enable, in_1[1]);
  and and_7 (and_7_out, Enable, in_1[0]);
  and and_8 (and_8_out, Enable, in_1[0]);
  not not_1 (not_1_out, and_2_out);
  not not_2 (not_2_out, and_4_out);
  not not_3 (not_3_out, and_6_out);
  not not_4 (not_4_out, and_8_out);
  not not_5 (not_5_out, Read_Write);
  and and_9 (and_9_out, not_5_out, Clk);
  S_R_Flip_Flop s_r_ff_1 (.S(and_1_out), .R(not_1_out), .clk(and_9_out), .Q(Nibble_Out[3]));  // open: reset, Qn, preset
  S_R_Flip_Flop s_r_ff_2 (.S(and_3_out), .R(not_2_out), .clk(and_9_out), .Q(Nibble_Out[2]));  // open: reset, Qn, preset
  S_R_Flip_Flop s_r_ff_3 (.S(and_5_out), .R(not_3_out), .clk(and_9_out), .Q(Nibble_Out[1]));  // open: reset, Qn, preset
  S_R_Flip_Flop s_r_ff_4 (.S(and_7_out), .R(not_4_out), .clk(and_9_out), .Q(Nibble_Out[0]));  // open: reset, Qn, preset
  // Probe on Nibble_Out

  // Notes on the sheet:
  //   When Read_Write = 1 performs read, otherwise performs write
endmodule

module ALU (
  input  [3:0] A,
  input  [3:0] B,
  input  AddSub,
  output [3:0] Aout,
  output Zero,
  output Overflow
);

  wire adder_2_cout, adder_3_cout, adder_4_cout, and_1_out, and_2_out, and_3_out, and_4_out, and_5_out,
       and_6_out, and_7_out, and_8_out, and_9_out, and_10_out, and_11_out, not_1_out, not_2_out, not_3_out,
       not_4_out, not_5_out, not_6_out, not_7_out, not_8_out, not_9_out, or_1_out, or_2_out, or_3_out,
       or_4_out, xor_1_out, xor_2_out, xor_3_out, xor_4_out;

  // Probe on A
  and and_1 (and_1_out, AddSub, B[3]);
  and and_2 (and_2_out, AddSub, B[2]);
  and and_3 (and_3_out, AddSub, B[1]);
  // Probe on B
  not not_1 (not_1_out, B[0]);
  not not_2 (not_2_out, AddSub);
  xor xor_1 (xor_1_out, not_2_out, not_1_out);
  and and_4 (and_4_out, AddSub, B[0]);
  and and_5 (and_5_out, xor_1_out, not_2_out);
  not not_3 (not_3_out, B[1]);
  not not_4 (not_4_out, B[2]);
  and and_6 (and_6_out, not_1_out, not_2_out);
  xor xor_2 (xor_2_out, and_6_out, not_3_out);
  and and_7 (and_7_out, and_6_out, not_3_out);
  xor xor_3 (xor_3_out, and_7_out, not_4_out);
  and and_8 (and_8_out, xor_3_out, not_2_out);
  and and_9 (and_9_out, xor_2_out, not_2_out);
  not not_5 (not_5_out, B[3]);
  and and_10 (and_10_out, not_4_out, and_7_out);
  xor xor_4 (xor_4_out, and_10_out, not_5_out);
  and and_11 (and_11_out, xor_4_out, not_2_out);
  // Probe on Aout
  or or_1 (or_1_out, and_5_out, and_4_out);
  or or_2 (or_2_out, and_3_out, and_9_out);
  or or_3 (or_3_out, and_2_out, and_8_out);
  or or_4 (or_4_out, and_1_out, and_11_out);
  Adder #(.width(1)) adder_1 (.a(A[3]), .b(or_4_out), .out(Aout[3]), .cin(adder_2_cout), .cout(Overflow));
  Adder #(.width(1)) adder_2 (.a(A[2]), .b(or_3_out), .out(Aout[2]), .cin(adder_3_cout), .cout(adder_2_cout));
  Adder #(.width(1)) adder_3 (.a(A[1]), .b(or_2_out), .out(Aout[1]), .cin(adder_4_cout), .cout(adder_3_cout));
  Adder #(.width(1)) adder_4 (.a(A[0]), .b(or_1_out), .out(Aout[0]), .cout(adder_4_cout));  // open: cin
  and and_12 (Zero, not_8_out, not_7_out, not_6_out, not_9_out);
  not not_6 (not_6_out, Aout[1]);
  not not_7 (not_7_out, Aout[2]);
  not not_8 (not_8_out, Aout[3]);
  not not_9 (not_9_out, Aout[0]);

  // Notes on the sheet:
  //   Laetitia Fesselier - 260791354
endmodule

module Inc (
  input  [1:0] DataIn,
  output [1:0] DataOut,
  output Overlfow
);

  wire adder_2_cout;

  // Probe on DataIn
  // Probe on DataOut
  Adder #(.width(1)) adder_1 (.a(1'b0), .b(DataIn[1]), .out(DataOut[1]), .cin(adder_2_cout), .cout(Overlfow));
  Adder #(.width(1)) adder_2 (.a(1'b1), .b(DataIn[0]), .out(DataOut[0]), .cout(adder_2_cout));  // open: cin
endmodule

module PC (
  input  [1:0] Data,
  input  Enabled,
  input  Clock,
  output [1:0] DataOut
);

  wire and_1_out, and_2_out, and_3_out, and_4_out;

  and and_1 (and_1_out, Enabled, Data[1]);
  and and_2 (and_2_out, ~Data[1], Enabled);  // AND_Gate
  and and_3 (and_3_out, Data[0], Enabled);
  and and_4 (and_4_out, ~Data[0], Enabled);  // AND_Gate
  S_R_Flip_Flop s_r_ff_1 (.S(and_1_out), .R(and_2_out), .clk(Clock), .Q(DataOut[1]));  // open: reset, Qn, preset
  S_R_Flip_Flop s_r_ff_2 (.S(and_3_out), .R(and_4_out), .clk(Clock), .Q(DataOut[0]));  // open: reset, Qn, preset
endmodule

module IR (
  input  [3:0] Data,
  input  Enabled,
  input  Clock,
  output [3:0] DataOut
);

  wire and_1_out, and_2_out, and_3_out, and_4_out, and_5_out, and_6_out, and_7_out, and_8_out;

  // Probe on Data
  and and_1 (and_1_out, Enabled, Data[0]);
  and and_2 (and_2_out, Enabled, ~Data[0]);  // AND_Gate
  and and_3 (and_3_out, Enabled, Data[1]);
  and and_4 (and_4_out, Enabled, ~Data[1]);  // AND_Gate
  and and_5 (and_5_out, Enabled, Data[2]);
  and and_6 (and_6_out, Enabled, ~Data[2]);  // AND_Gate
  and and_7 (and_7_out, Enabled, Data[3]);
  and and_8 (and_8_out, Enabled, ~Data[3]);  // AND_Gate
  S_R_Flip_Flop s_r_ff_1 (.S(and_1_out), .R(and_2_out), .clk(Clock), .Q(DataOut[0]));  // open: reset, Qn, preset
  S_R_Flip_Flop s_r_ff_2 (.S(and_3_out), .R(and_4_out), .clk(Clock), .Q(DataOut[1]));  // open: reset, Qn, preset
  S_R_Flip_Flop s_r_ff_3 (.S(and_5_out), .R(and_6_out), .clk(Clock), .Q(DataOut[2]));  // open: reset, Qn, preset
  S_R_Flip_Flop s_r_ff_4 (.S(and_7_out), .R(and_8_out), .clk(Clock), .Q(DataOut[3]));  // open: reset, Qn, preset
  // Probe on DataOut
endmodule

module Nibbles_RAM (
  input  [3:0] Data,
  input  Read_Write,
  input  [1:0] Address,
  input  Clk,
  output [3:0] RAM_OUT,
  output [3:0] out_6,
  output [3:0] out_7,
  output [3:0] out_8,
  output [3:0] out_9
);

  wire and_1_out, and_2_out, and_3_out, and_4_out, and_5_out, and_6_out, and_7_out, and_8_out, and_9_out,
       and_10_out, and_11_out, and_12_out, and_13_out, and_14_out, and_15_out, and_16_out, and_17_out,
       and_18_out, and_19_out, and_20_out, not_1_out, not_2_out, not_3_out, not_4_out, or_5_out, or_6_out,
       or_7_out, or_8_out, or_9_out, or_10_out, or_11_out, or_12_out;

  not not_1 (not_1_out, Address[1]);
  and and_1 (and_1_out, not_1_out, not_2_out);
  not not_2 (not_2_out, Address[0]);
  not not_3 (not_3_out, Address[1]);
  and and_2 (and_2_out, not_3_out, Address[0]);
  and and_3 (and_3_out, Address[1], not_4_out);
  not not_4 (not_4_out, Address[0]);
  and and_4 (and_4_out, Address[0], Address[1]);
  Nibble nibble_1 (.in_1(Data), .Read_Write(Read_Write), .Clk(Clk), .Enable(and_1_out), .Nibble_Out(out_6));
  Nibble nibble_2 (.in_1(Data), .Read_Write(Read_Write), .Clk(Clk), .Enable(and_2_out), .Nibble_Out(out_7));
  Nibble nibble_3 (.in_1(Data), .Read_Write(Read_Write), .Clk(Clk), .Enable(and_3_out), .Nibble_Out(out_8));
  Nibble nibble_4 (.in_1(Data), .Read_Write(Read_Write), .Clk(Clk), .Enable(and_4_out), .Nibble_Out(out_9));
  // Probe on Address
  and and_5 (and_5_out, and_1_out, out_6[0]);
  and and_6 (and_6_out, and_1_out, out_6[1]);
  and and_7 (and_7_out, and_1_out, out_6[2]);
  and and_8 (and_8_out, and_1_out, out_6[3]);
  and and_9 (and_9_out, and_2_out, out_7[0]);
  and and_10 (and_10_out, and_2_out, out_7[1]);
  and and_11 (and_11_out, and_2_out, out_7[2]);
  and and_12 (and_12_out, and_2_out, out_7[3]);
  and and_13 (and_13_out, and_3_out, out_8[0]);
  and and_14 (and_14_out, and_3_out, out_8[1]);
  and and_15 (and_15_out, and_3_out, out_8[2]);
  and and_16 (and_16_out, and_3_out, out_8[3]);
  and and_17 (and_17_out, and_4_out, out_9[0]);
  and and_18 (and_18_out, and_4_out, out_9[1]);
  and and_19 (and_19_out, and_4_out, out_9[2]);
  and and_20 (and_20_out, and_4_out, out_9[3]);
  // Probe on RAM_OUT
  or or_1 (RAM_OUT[0], and_5_out, or_11_out);
  or or_2 (RAM_OUT[1], and_6_out, or_5_out);
  or or_3 (RAM_OUT[2], and_7_out, or_6_out);
  or or_4 (RAM_OUT[3], and_8_out, or_7_out);
  or or_5 (or_5_out, and_10_out, or_8_out);
  or or_6 (or_6_out, and_11_out, or_9_out);
  or or_7 (or_7_out, and_12_out, or_10_out);
  or or_8 (or_8_out, and_14_out, and_18_out);
  or or_9 (or_9_out, and_15_out, and_19_out);
  or or_10 (or_10_out, and_16_out, and_20_out);
  or or_11 (or_11_out, and_9_out, or_12_out);
  or or_12 (or_12_out, and_13_out, and_17_out);

  // Notes on the sheet:
  //   When Read_Write = 1 performs read, otherwise performs write
endmodule

module Steps (
  input  [1:0] Data,
  input  Enable,
  input  Clk,
  output [1:0] Dataout
);

  wire and_1_out, and_2_out, and_3_out, and_4_out;

  and and_1 (and_1_out, Enable, Data[0]);
  and and_2 (and_2_out, Enable, ~Data[0]);  // AND_Gate
  and and_3 (and_3_out, Enable, Data[1]);
  and and_4 (and_4_out, Enable, ~Data[1]);  // AND_Gate
  S_R_Flip_Flop s_r_ff_1 (.S(and_1_out), .R(and_2_out), .clk(Clk), .Q(Dataout[0]));  // open: reset, Qn, preset
  S_R_Flip_Flop s_r_ff_2 (.S(and_3_out), .R(and_4_out), .clk(Clk), .Q(Dataout[1]));  // open: reset, Qn, preset
endmodule

module Aout (
  input  [3:0] DataIn,
  input  Clk,
  input  Enabled,
  output [3:0] DataOut
);

  wire and_1_out, and_2_out, and_3_out, and_4_out, and_5_out, and_6_out, and_7_out, and_8_out, not_1_out,
       not_2_out, not_3_out, not_4_out;

  not not_1 (not_1_out, DataIn[2]);
  not not_2 (not_2_out, DataIn[3]);
  // Probe on DataIn
  not not_3 (not_3_out, DataIn[0]);
  not not_4 (not_4_out, DataIn[1]);
  and and_1 (and_1_out, DataIn[0], Enabled);
  and and_2 (and_2_out, not_3_out, Enabled);
  and and_3 (and_3_out, DataIn[1], Enabled);
  and and_4 (and_4_out, not_4_out, Enabled);
  and and_5 (and_5_out, DataIn[2], Enabled);
  and and_6 (and_6_out, not_1_out, Enabled);
  and and_7 (and_7_out, DataIn[3], Enabled);
  and and_8 (and_8_out, not_2_out, Enabled);
  S_R_Flip_Flop s_r_ff_1 (.S(and_1_out), .R(and_2_out), .clk(Clk), .Q(DataOut[0]));  // open: reset, Qn, preset
  S_R_Flip_Flop s_r_ff_2 (.S(and_3_out), .R(and_4_out), .clk(Clk), .Q(DataOut[1]));  // open: reset, Qn, preset
  S_R_Flip_Flop s_r_ff_3 (.S(and_5_out), .R(and_6_out), .clk(Clk), .Q(DataOut[2]));  // open: reset, Qn, preset
  S_R_Flip_Flop s_r_ff_4 (.S(and_7_out), .R(and_8_out), .clk(Clk), .Q(DataOut[3]));  // open: reset, Qn, preset
  // Probe on DataOut
endmodule
